// Logisim project cpu.circ as structural Verilog
module ALU_FullAdder (
  input  Cin,
  input  A,
  input  B,
  output S,
  output Cout
);

  wire and_1_out, and_2_out, xor_1_out;

  and and_1 (and_1_out, A, B);
  xor xor_1 (xor_1_out, A, B);
  xor xor_2 (S, Cin, xor_1_out);
  and and_2 (and_2_out, Cin, xor_1_out);
  or or_1 (Cout, and_2_out, and_1_out);
endmodule

module ALU_Adder4 (
  input  Cin,
  input  [3:0] A,
  input  [3:0] B,
  output [3:0] S,
  output Cout
);

  wire alu_fulladder_1_cout, alu_fulladder_2_cout, alu_fulladder_3_cout;

  ALU_FullAdder alu_fulladder_1 (.Cin(Cin), .A(A[0]), .B(B[0]), .S(S[0]), .Cout(alu_fulladder_1_cout));
  ALU_FullAdder alu_fulladder_2 (.Cin(alu_fulladder_1_cout), .A(A[1]), .B(B[1]), .S(S[1]), .Cout(alu_fulladder_2_cout));
  ALU_FullAdder alu_fulladder_3 (.Cin(alu_fulladder_2_cout), .A(A[2]), .B(B[2]), .S(S[2]), .Cout(alu_fulladder_3_cout));
  ALU_FullAdder alu_fulladder_4 (.Cin(alu_fulladder_3_cout), .A(A[3]), .B(B[3]), .S(S[3]), .Cout(Cout));
endmodule

module ALU_Aritmetica_16b (
  input  [15:0] A,
  input  [15:0] B,
  input  SUB,
  output [15:0] S,
  output Cout
);

  wire alu_adder4_1_cout, alu_adder4_2_cout, alu_adder4_3_cout;
  wire [3:0] xor_1_out;
  wire [15:0] bit_extender_1_out;
  wire [15:4] xor_1_out_2;

  assign bit_extender_1_out = {{15{SUB}}, SUB};  // Bit_Extender bit_extender_1
  assign {xor_1_out_2, xor_1_out} = B ^ bit_extender_1_out;  // XOR_Gate xor_1, 16 bits wide
  ALU_Adder4 alu_adder4_1 (.Cin(SUB), .A(A[3:0]), .B(xor_1_out), .S(S[3:0]), .Cout(alu_adder4_1_cout));
  ALU_Adder4 alu_adder4_2 (
    .Cin(alu_adder4_1_cout), .A(A[7:4]), .B(xor_1_out_2[7:4]), .S(S[7:4]), .Cout(alu_adder4_2_cout));
  ALU_Adder4 alu_adder4_3 (
    .Cin(alu_adder4_2_cout), .A(A[11:8]), .B(xor_1_out_2[11:8]), .S(S[11:8]), .Cout(alu_adder4_3_cout));
  ALU_Adder4 alu_adder4_4 (.Cin(alu_adder4_3_cout), .A(A[15:12]), .B(xor_1_out_2[15:12]), .S(S[15:12]), .Cout(Cout));
endmodule

module ALU_SLL16b (
  input  [15:0] A,
  input  [3:0] B,
  output [15:0] S
);

  wire [15:0] multiplexer_1_out, multiplexer_2_out, multiplexer_3_out;

  Multiplexer #(.width(16)) multiplexer_1 (.in0(A), .in1({A[14:0], 1'b0}), .out(multiplexer_1_out), .sel(B[0]));
  Multiplexer #(.width(16)) multiplexer_2 (
    .in0(multiplexer_1_out), .in1({multiplexer_1_out[13:0], 2'b00}), .out(multiplexer_2_out), .sel(B[1]));
  Multiplexer #(.width(16)) multiplexer_3 (
    .in0(multiplexer_2_out), .in1({multiplexer_2_out[11:0], 4'b0000}), .out(multiplexer_3_out), .sel(B[2]));
  Multiplexer #(.width(16)) multiplexer_4 (
    .in0(multiplexer_3_out), .in1({multiplexer_3_out[7:0], {8{1'b0}}}), .out(S), .sel(B[3]));
endmodule

module ALU_SRL16b (
  input  [15:0] A,
  input  [3:0] B,
  output [15:0] S
);

  wire [15:0] multiplexer_1_out, multiplexer_2_out, multiplexer_3_out;

  Multiplexer #(.width(16)) multiplexer_1 (.in0(A), .in1({1'b0, A[15:1]}), .out(multiplexer_1_out), .sel(B[0]));
  Multiplexer #(.width(16)) multiplexer_2 (
    .in0(multiplexer_1_out), .in1({2'b00, multiplexer_1_out[15:2]}), .out(multiplexer_2_out), .sel(B[1]));
  Multiplexer #(.width(16)) multiplexer_3 (
    .in0(multiplexer_2_out), .in1({4'b0000, multiplexer_2_out[15:4]}), .out(multiplexer_3_out), .sel(B[2]));
  Multiplexer #(.width(16)) multiplexer_4 (
    .in0(multiplexer_3_out), .in1({{8{1'b0}}, multiplexer_3_out[15:8]}), .out(S), .sel(B[3]));
endmodule

module ALU_SRA16b (
  input  [15:0] A,
  input  [3:0] B,
  output [15:0] S
);

  wire [15:0] multiplexer_1_out, multiplexer_2_out, multiplexer_3_out;

  Multiplexer #(.width(16)) multiplexer_1 (.in0(A), .in1({{2{A[15]}}, A[14:1]}), .out(multiplexer_1_out), .sel(B[0]));
  Multiplexer #(.width(16)) multiplexer_2 (
    .in0(multiplexer_1_out), .in1({{2{A[15]}}, multiplexer_1_out[15:2]}), .out(multiplexer_2_out), .sel(B[1]));
  Multiplexer #(.width(16)) multiplexer_3 (
    .in0(multiplexer_2_out), .in1({{4{A[15]}}, multiplexer_2_out[15:4]}), .out(multiplexer_3_out), .sel(B[2]));
  Multiplexer #(.width(16)) multiplexer_4 (
    .in0(multiplexer_3_out), .in1({{8{A[15]}}, multiplexer_3_out[15:8]}), .out(S), .sel(B[3]));
endmodule

module ALU_Main (
  input  [15:0] A,
  input  [15:0] B,
  input  [3:0] ALU_Control,
  output Z,
  output SLT,
  output V,
  output N
);

  wire not_1_out, or_2_out, or_3_out, or_4_out, or_5_out, xnor_1_out, xor_2_out;
  wire [3:0] alu_aritmetica_16b_1_s, alu_aritmetica_16b_1_s_2, alu_aritmetica_16b_1_s_3,
       alu_aritmetica_16b_1_s_4;
  wire [15:0] multiplexer_1_out;

  ALU_Aritmetica_16b alu_aritmetica_16b_1 (.S({alu_aritmetica_16b_1_s_4, alu_aritmetica_16b_1_s_3, alu_aritmetica_16b_1_s_2, alu_aritmetica_16b_1_s}));  // open: A, B, SUB, Cout
  // AND_Gate and_1 is placed but not wired
  // OR_Gate or_1 is placed but not wired
  // XOR_Gate xor_1 is placed but not wired
  or or_2 (or_2_out, alu_aritmetica_16b_1_s_4[0], alu_aritmetica_16b_1_s_4[1], alu_aritmetica_16b_1_s_4[2], alu_aritmetica_16b_1_s_4[3]);
  or or_3 (or_3_out, alu_aritmetica_16b_1_s_3[0], alu_aritmetica_16b_1_s_3[1], alu_aritmetica_16b_1_s_3[2], alu_aritmetica_16b_1_s_3[3]);
  or or_4 (or_4_out, alu_aritmetica_16b_1_s_2[0], alu_aritmetica_16b_1_s_2[1], alu_aritmetica_16b_1_s_2[2], alu_aritmetica_16b_1_s_2[3]);
  or or_5 (or_5_out, alu_aritmetica_16b_1_s[0], alu_aritmetica_16b_1_s[1], alu_aritmetica_16b_1_s[2], alu_aritmetica_16b_1_s[3]);
  nor nor_1 (Z, or_2_out, or_3_out, or_4_out, or_5_out);
  and and_2 (N, 1'b1, alu_aritmetica_16b_1_s_4[3]);
  Multiplexer #(.select(4), .width(16)) multiplexer_1 (
    .in0({alu_aritmetica_16b_1_s_4, alu_aritmetica_16b_1_s_3, alu_aritmetica_16b_1_s_2, alu_aritmetica_16b_1_s}),
    .in1({alu_aritmetica_16b_1_s_4, alu_aritmetica_16b_1_s_3, alu_aritmetica_16b_1_s_2, alu_aritmetica_16b_1_s}),
    .out(multiplexer_1_out), .sel(ALU_Control));  // open: in2, in3, in4, in5, in6, in7, in8, in9, in10, in11, in12, in13, in14, in15
  not not_1 (not_1_out, B[15]);
  xnor xnor_1 (xnor_1_out, A[15], not_1_out);
  xor xor_2 (xor_2_out, A[15], alu_aritmetica_16b_1_s_4[3]);
  and and_3 (V, xnor_1_out, xor_2_out);
  xor xor_3 (SLT, N, V);

  // Notes on the sheet:
  //   Zero Flag Calc
  //   Negative Flag
  //   000 ADD
  //   001 SUB
  //   010 AND
  //   011 OR
  //   100 XOR
  //   101 SLL
  //   110 SRL
  //   111 SLT
endmodule

module ALU_NEWMain (
  input  [15:0] A,
  input  [15:0] B,
  input  [3:0] ALU_Control,
  output Z,
  output V,
  output N,
  output C,
  output [15:0] out_8
);

  wire Cout, xor_2_out;
  wire [15:0] alu_sll16b_1_s, alu_sra16b_1_s, alu_srl16b_1_s, and_1_out, bit_extender_1_out, or_1_out, Sout,
       xor_1_out;

  assign and_1_out = A;  // AND_Gate and_1, 16 bits wide AND_Gate
  assign or_1_out = B;  // OR_Gate or_1, 16 bits wide OR_Gate
  ALU_SLL16b alu_sll16b_1 (.A(A), .S(alu_sll16b_1_s));  // open: B
  ALU_SRL16b alu_srl16b_1 (.A(A), .S(alu_srl16b_1_s));  // open: B
  ALU_SRA16b alu_sra16b_1 (.A(A), .S(alu_sra16b_1_s));  // open: B
  ALU_Flags alu_flags_1 (.Cin(Cout), .A(A), .B(B), .Sin(Sout), .Z(Z), .V(V), .N(N), .C(C));
  ALU_Aritmetica_16b alu_aritmetica_16b_1 (.A(A), .B(B), .SUB(ALU_Control[0]), .Cout(Cout), .S(Sout));
  assign xor_1_out = A ^ A;  // XOR_Gate xor_1, 16 bits wide
  xor xor_2 (xor_2_out, N, V);
  assign bit_extender_1_out = {{15{xor_2_out}}, xor_2_out};  // Bit_Extender bit_extender_1
  Multiplexer #(.select(4), .width(16)) multiplexer_1 (
    .in0(Sout), .in1(Sout), .in2(and_1_out), .in3(or_1_out), .in4(xor_1_out), .in5(alu_sll16b_1_s),
    .in6(alu_srl16b_1_s), .in7(bit_extender_1_out), .in8(alu_sra16b_1_s), .out(out_8), .sel(ALU_Control));  // open: in9, in10, in11, in12, in13, in14, in15

  // Other names for the same wires on the sheet: B0_Opcode = ALU_Control[0]

  // Notes on the sheet:
  //   ALU_SLT
  //   0000 ADD
  //   0001 SUB
  //   0010 AND
  //   0011 OR
  //   0100 XOR
  //   0101 SLL
  //   0110 SRL
  //   0111 SLT
  //   1000 SRA
endmodule

module ALU_Flags (
  input  [15:0] A,
  input  [15:0] B,
  input  [15:0] Sin,
  input  Cin,
  output Z,
  output V,
  output N,
  output C
);

  wire or_1_out, or_2_out, or_3_out, or_4_out, xnor_1_out, xor_1_out;

  or or_1 (or_1_out, Sin[0], Sin[1], Sin[2], Sin[3]);
  or or_2 (or_2_out, Sin[4], Sin[5], Sin[6], Sin[7]);
  or or_3 (or_3_out, Sin[8], Sin[9], Sin[10], Sin[11]);
  or or_4 (or_4_out, Sin[12], Sin[13], Sin[14], Sin[15]);
  xnor xnor_1 (xnor_1_out, A[15], B[15]);
  xor xor_1 (xor_1_out, A[15], Sin[15]);
  nor nor_1 (Z, or_1_out, or_2_out, or_3_out, or_4_out);
  and and_1 (V, xnor_1_out, xor_1_out);
  and and_2 (N, 1'b1, Sin[15]);

  assign C = Cin;
endmodule
