// Logisim project program_counter.circ as structural Verilog: 1 circuit, main circuit PC_Main
module PC_Main (
  input  [15:0] Adress_Out,
  input  Halt,
  input  CLK,
  input  Reset,
  input  [15:0] Adress_Write,
  input  JR_Enable,
  input  PC_Src,
  input  [15:0] JR_Adress
);

  wire not_1_out;
  wire [15:0] adder_1_out, multiplexer_1_out, multiplexer_2_out;

  Multiplexer #(.width(16)) multiplexer_1 (
    .in0(multiplexer_2_out), .in1(JR_Adress), .out(multiplexer_1_out), .sel(JR_Enable));
  Register #(.width(16)) register_1 (.D(multiplexer_1_out), .en(not_1_out), .clk(CLK), .Q(Adress_Out), .clr(Reset));
  not not_1 (not_1_out, Halt);
  Multiplexer #(.width(16)) multiplexer_2 (
    .in0(adder_1_out), .in1(Adress_Write), .out(multiplexer_2_out), .sel(PC_Src));
  Adder #(.width(16)) adder_1 (.a(Adress_Out), .b(16'h1), .out(adder_1_out));  // open: cin, cout
endmodule
